# Fritzing sketch submarine (saved by Fritzing 0.9.2b)
breadboards: 1

parts:
  Bottom = Basic Servo
  U1 = L9110 H-bridge module [part_number="L9110 H-bridge"]
  Navigation_body_IR_receiver = IR Receiver Breakout [package=PCB]
  6_0_V = Battery Holders [package=battery-aa]
  Motor_controller = Arduino Nano (Rev3.0)
  Ballast = DC Motor
  Propeller = DC Motor
  6_0_V_2 = Battery Holders [package=battery-aa]
  6_0_V_3 = Battery Holders [package=battery-aa]
  Top = Basic Servo
  6_0_V_4 = Battery Holders [package=battery-aa]
  6_0_V_5 = Battery Holders [package=battery-aa]
  Front = Basic Servo
  Right = Basic Servo
  6_0_V_6 = Battery Holders [package=battery-aa]
  Left = Basic Servo
  5_6_V = Battery Holders [package=battery-aa]
  part = Humidity Sensor - HIH-4030 Breakout

nets:
  N1: Bottom.gnd, 6_0_V_2.-
  N2: Bottom.vcc, 6_0_V_2.+
  N3: Bottom.pulse, Motor_controller.D2
  N4: U1.B-IA, Motor_controller.D8
  N5: U1.B-IB, Motor_controller.D7
  N6: U1.GND, 6_0_V.-
  N7: U1.VCC, 6_0_V.+
  N8: U1.A-IA, Motor_controller.D10
  N9: U1.A-IB, Motor_controller.D9
  N10: U1.MOTOR_A-A, Ballast.pin_1
  N11: U1.MOTOR_A-B, Ballast.pin_2
  N12: U1.MOTOR_B-A, Propeller.pin_2
  N13: U1.MOTOR_B-B, Propeller.pin_1
  GND: Navigation_body_IR_receiver.GND, Motor_controller.GND, 5_6_V.-, part.GND
  N14: Navigation_body_IR_receiver.OUT, Motor_controller.D11/MOSI
  VCC: Navigation_body_IR_receiver.VCC, Motor_controller.5V
  N15: Motor_controller.D3, Top.pulse
  N16: Motor_controller.D4, Left.pulse
  N17: Motor_controller.D5, Right.pulse
  N18: Motor_controller.D6, Front.pulse
  N19: Motor_controller.VIN, 5_6_V.+
  N20: Motor_controller.A1, part.OUT
  3V3: Motor_controller.3V3, part.VCC
  N21: 6_0_V_3.-, Top.gnd
  N22: 6_0_V_3.+, Top.vcc
  N23: 6_0_V_4.-, Right.gnd
  N24: 6_0_V_4.+, Right.vcc
  N25: 6_0_V_5.-, Front.gnd
  N26: 6_0_V_5.+, Front.vcc
  N27: 6_0_V_6.-, Left.gnd
  N28: 6_0_V_6.+, Left.vcc

notes:
  Rudders
  Hydroplanes
